# Fritzing sketch step_00_led (saved by Fritzing 0.9.9b)
breadboards: 1

parts:
  LED1 = LED - 5mm [color="Red (633nm)" current=0.030 package="5 mm [THT]"]
  R1 = Resistor [tolerance=±5% resistance=220 power=0.25 package=THT]
  WeMos_D1_Mini1 = WeMos D1 Mini  # not connected

nets:
  N1: LED1.cathode, R1.Pin_1
