# Fritzing sketch step_40_button_input (saved by Fritzing 0.9.9b)
breadboards: 1

parts:
  R1 = Resistor [tolerance=±5% resistance=220 package="0805 [SMD]"]
  S1 = Pushbutton [package="[THT]"]
  LED1 = LED - 5mm [color="Red (633nm)" current=0.030 package="5 mm [THT]"]  # not connected
  WeMos_D1_Mini1 = WeMos D1 Mini  # not connected

nets:
  N1: R1.Pin_0, S1.Pin_3, S1.Pin_4
  N2: S1.Pin_1, S1.Pin_2
